// Logisim project evolution_D_FF.circ as structural Verilog
module SR_Latch (
  input  set,
  input  reset,
  input  enable,
  output oput
);

  wire and_1_out, and_2_out, not_1_out, or_1_out;

  and and_1 (and_1_out, set, enable);
  and and_2 (and_2_out, enable, reset);
  or or_1 (or_1_out, and_1_out, oput);
  not not_1 (not_1_out, and_2_out);
  and and_3 (oput, or_1_out, not_1_out);
endmodule

module D_Latch (
  input  data,
  input  enable,
  output oput
);

  wire not_1_out;

  not not_1 (not_1_out, data);
  SR_Latch sr_latch_1 (.set(data), .reset(not_1_out), .enable(enable), .oput(oput));
endmodule

module D_FF (
  input  in_1,
  input  in_2,
  output out_3
);

  wire d_latch_1_oput, not_1_out;

  not not_1 (not_1_out, in_2);
  D_Latch d_latch_1 (.data(in_1), .enable(not_1_out), .oput(d_latch_1_oput));
  D_Latch d_latch_2 (.data(d_latch_1_oput), .enable(in_2), .oput(out_3));
endmodule
